# Fritzing sketch EsquemaCompleto (saved by Fritzing 1.0.5)
breadboards: 2

parts:
  Componente1 = Arduino Uno (Rev3) - ICSP
  S1 = KY-026
  DHT1 = DHT11 Humitidy and Temperature Sensor
  OLED1 = OLED 128x64 I2C Monochrome Display
  S2 = 0.91 inch OLED I2C Display 128 x 32 Pixels
  Mod1 = KY-016 RGB Full Color LED Module [package="Breakout board"]
  Mod2 = KY-016 RGB Full Color LED Module [package="Breakout board"]
  Water_Level_Sensor1 = Water Level Sensor
  M1 = DC Motor [voltage_(max)=6V voltage_(min)=3V]
  Componente2 = PN532 Elechouse RFID NFC Module V3
  Q1 = NPN-Transistor [package="SOT-23 [SMD]"]
  WeMos_D1_Mini1 = WeMos D1 Mini
  J3 = Piezo Speaker
  R1 = Resistor [tolerance=±5% resistance=220 package="2512 [SMD]"]
  Componente3 = Arduino Uno (Rev3) - ICSP
  J2 = Basic Servo
  WeMos_D1_Mini2 = WeMos D1 Mini
  J4 = Piezo Speaker

nets:
  N1: Componente1.D9_PWM, J4.pin2
  N2: Componente1.GND, Componente2.GND#1, WeMos_D1_Mini2.G, J4.pin1
  N3: Componente1.D0/RX, WeMos_D1_Mini2.TX
  N4: Componente1.D1/TX, WeMos_D1_Mini2.RX
  N5: Componente1.D3_PWM, Componente2.SDA
  N6: Componente1.D4, Componente2.SCL
  5V: Componente1.5V, Componente2.VCC, WeMos_D1_Mini2.5V
  GND: S1.pin2, DHT1.GND, OLED1.GND, S2.GND, Mod1.-, Mod2.-, Water_Level_Sensor1.GND, Q1.1, WeMos_D1_Mini1.G, J3.pin1, Componente3.GND, J2.gnd
  VCC: S1.pin3, DHT1.VDD, OLED1.VDD, S2.VCC, Water_Level_Sensor1.VCC, M1.pin_2, WeMos_D1_Mini1.5V, Componente3.5V, J2.vcc
  N7: S1.pin4, Componente3.D4
  N8: DHT1.DATA, Componente3.D2
  N9: OLED1.SCK, S2.SCL, Componente3.A5/SCL
  N10: OLED1.SDA, S2.SDA, Componente3.A4/SDA
  N11: Mod1.R, Mod2.R, Componente3.D9_PWM
  N12: Mod1.G, Mod2.G, Componente3.D10_PWM/SS
  N13: Mod1.B, Mod2.B, Componente3.D11_PWM/MOSI
  N14: Water_Level_Sensor1.SIG, Componente3.A0
  N15: M1.pin_1, Q1.2
  N16: Q1.0, R1.Pin_1
  N17: WeMos_D1_Mini1.RX, Componente3.D1/TX
  N18: WeMos_D1_Mini1.TX, Componente3.D0/RX
  N19: J3.pin2, Componente3.D3_PWM
  N20: R1.Pin_0, Componente3.D6_PWM
  N21: Componente3.D5_PWM, J2.pulse

custom parts:
  KY-026: ky-026 flame sensor module
  DHT11 Humitidy and Temperature Sensor: DHT11 Humidity and Temperature Sensor
  KY-016 RGB Full Color LED Module: KY-016 Arduino full color 5mm RGB LED, different colors can be obtained by mixing the three primary colors.
  Water Level Sensor: A water level sensor. This sensor operates at 3V to 5V. The Sig (signal) pin outputs an analogue signal that is in proportion to the amount of water in contact with the sensor.
  PN532 Elechouse RFID NFC Module V3: NFC is a popular technology in recent years. We often heard this work while smart phone company such as Samsung or HTC introduces their latest high-end phones. Almost all the high-end phone in the market support NFC. Near field communication (NFC) is a set of standards for smart phones and similar devices to establish radio communication with each other by touching them together or bringing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
